// Logisim project CPU(S-MIPS).circ as structural Verilog: 1 circuit, main circuit S-MIPS
module S_MIPS (
  input  [31:0] RAM_Out_0,
  input  [31:0] RAM_Out_1,
  input  [31:0] RAM_Out_2,
  input  [31:0] RAM_Out_3,
  input  [3:0] Read_Time,
  input  [3:0] Write_Time,
  input  Reset,
  input  Clock,
  input  Kbd_Available,
  input  [6:0] Kbd_ASCII_Data,
  output [31:0] RAM_In_0,
  output [31:0] RAM_In_1,
  output [31:0] RAM_In_2,
  output [31:0] RAM_In_3,
  output Halt,
  output [15:0] Address,
  output Kbd_Enable,
  output Kbd_Clear,
  output TTY_Enable,
  output [6:0] TTY_ASCII_Data,
  output [3:0] Mask,
  output nRead_Write,
  output Chip_Select
);

  wire en_MC, Fetch, inst_R_W, Ram_Ready, rnd_kbd;
  wire [2:0] S_FC;
  wire [3:0] ALU_OP, mask_t;
  wire [5:0] FuncCode, OpCode;
  wire [15:0] inst_addrs;
  wire [17:0] SelectorCodes;
  wire [31:0] inp_Word, inst, MemoryAddress, MemoryData, Out_Word;

  // Control_Unit control_unit_1: pin names not known; wires that end beside it: Reset, Ram_Ready, FuncCode, OpCode, Reset, Reset, S_FC, ALU_OP, SelectorCodes, rnd_kbd, TTY_Enable
  // Memory_Controller memory_controller_1: pin names not known; wires that end beside it: Write_Time, Read_Time, Ram_Ready, Chip_Select, en_MC, nRead_Write, inst_R_W, RAM_Out_3, RAM_In_3, RAM_Out_2, RAM_In_2, RAM_Out_1, RAM_In_1, RAM_Out_0, RAM_In_0, mask_t, Mask, inp_Word, Out_Word, inst_addrs, Address
  // DataPath datapath_1: pin names not known; wires that end beside it: Reset, Out_Word, inst, Kbd_ASCII_Data, Kbd_Available, Fetch, SelectorCodes, rnd_kbd, ALU_OP, S_FC, MemoryAddress, TTY_ASCII_Data, FuncCode, OpCode, MemoryData

  // Other names for the same wires on the sheet: CLK = Clock; CS = Chip_Select; KBD_AVAIL = Kbd_Available;
  //   KBD_CLR = Kbd_Clear; KBD_DATA[6:0] = Kbd_ASCII_Data; RAM_A[15:0] = Address; RAM_MASK[3:0] = Mask;
  //   RI0[31:0] = RAM_In_0; RI1[31:0] = RAM_In_1; RI2[31:0] = RAM_In_2; RI_3[31:0] = RAM_In_3; RO0[31:0] = RAM_Out_0;
  //   RO1[31:0] = RAM_Out_1; RO2[31:0] = RAM_Out_2; RO3[31:0] = RAM_Out_3; RST = Reset; RW = nRead_Write; STOP = Halt;
  //   TTY_DATA[6:0] = TTY_ASCII_Data

  // Notes on the sheet:
  //   RAM TIMING
  //   KEYBOARD
  //   DATA FROM RAM
  //   RAM ADDRESS
  //   KEYBOARD
  //   TTY
  //   DATA WRITE MASK
  //   RAM CONTROL
  //   DATA TO RAM
endmodule
