// Logisim project Control_Unit.circ as structural Verilog: 1 circuit, main circuit Control Unit
module Control_Unit (
  input  [5:0] FuncCode,
  input  [5:0] OpCode,
  input  START,
  input  Clock,
  input  RamReady,
  output [17:0] SelectorCodes,
  output [2:0] FC_Selector,
  output [3:0] ALU_Op,
  output fetch,
  output rnd_kbd_Selector,
  output TTY_Enable,
  output ReadInstruction,
  output ChipSelect,
  output R_W,
  output halt,
  output kbd_Enable,
  output RESET
);

  wire CS0, CS1, CS2, CS3, CS4, demultiplexer_1_out0, demultiplexer_1_out1, demultiplexer_2_out0,
       demultiplexer_3_out0, demultiplexer_4_out0, demultiplexer_5_out0, demultiplexer_6_out0, FETCH_q,
       IDLE_q, Load, Main, or_1_out, Pop, Push, R1, R2, R2_1, R3, R4, ReadMemory_2_q, ReadMemory_q, Store,
       WriteMemory_2_q;
  wire [1:0] SS_Code;
  wire [17:0] F_S_Codes;

  or or_1 (or_1_out, demultiplexer_1_out1, halt);
  or or_2 (R_W, Push, Store);
  Demultiplexer #(.enable("false")) demultiplexer_1 (
    .out0(demultiplexer_1_out0), .out1(demultiplexer_1_out1), .in(IDLE_q), .sel(START));
  D_Flip_Flop IDLE (.clk(Clock), .D(or_1_out), .Q(IDLE_q), .preset(START));  // open: Qn, en, reset
  Priority_Encoder #(.select(2)) priority_encoder_1 (
    .in0(R1), .in1(R2), .in2(R3), .in3(Main), .out(SS_Code));  // open: gs, en_out, en_in
  or or_3 (CS1, demultiplexer_2_out0, Pop);
  or or_4 (CS2, demultiplexer_3_out0, Push);
  or or_5 (CS3, demultiplexer_4_out0, Load);
  or or_6 (CS4, demultiplexer_5_out0, Store);
  or or_7 (fetch, R1, R2_1, R3, R4, Main);
  or or_8 (CS0, demultiplexer_6_out0, fetch, demultiplexer_1_out0);
  D_Flip_Flop ReadMemory (.clk(Clock), .D(CS1), .Q(ReadMemory_q));  // open: Qn, preset, en, reset
  D_Flip_Flop WriteMemory (.clk(Clock), .D(CS2), .Q(R2));  // open: Qn, preset, en, reset
  D_Flip_Flop ReadMemory_2 (.clk(Clock), .D(CS3), .Q(ReadMemory_2_q));  // open: Qn, preset, en, reset
  D_Flip_Flop WriteMemory_2 (.clk(Clock), .D(CS4), .Q(WriteMemory_2_q));  // open: Qn, preset, en, reset
  D_Flip_Flop u_FETCH (.clk(Clock), .D(CS0), .Q(FETCH_q), .reset(START));  // open: Qn, preset, en
  Demultiplexer #(.enable("false")) demultiplexer_2 (
    .out0(demultiplexer_2_out0), .out1(R1), .in(ReadMemory_q), .sel(RamReady));
  Demultiplexer #(.enable("false")) demultiplexer_3 (.out0(demultiplexer_3_out0), .out1(R2_1), .in(R2), .sel(RamReady));
  Demultiplexer #(.enable("false")) demultiplexer_4 (
    .out0(demultiplexer_4_out0), .out1(R3), .in(ReadMemory_2_q), .sel(RamReady));
  Demultiplexer #(.enable("false")) demultiplexer_5 (
    .out0(demultiplexer_5_out0), .out1(R4), .in(WriteMemory_2_q), .sel(RamReady));
  Demultiplexer #(.enable("false")) demultiplexer_6 (
    .out0(demultiplexer_6_out0), .out1(ReadInstruction), .in(FETCH_q), .sel(RamReady));
  Multiplexer #(.select(2), .width(18), .enable("false")) multiplexer_1 (
    .in0(SelectorCodes), .in1(18'h20024), .in2(18'h10), .in3(18'h20021), .out(F_S_Codes), .sel(SS_Code));
  Switcher_CU switcher_cu_1 (
    .kbd_rnd(rnd_kbd_Selector), .FuncCode(FuncCode), .OpCode(OpCode), .ALU_OP(ALU_Op),
    .TTY_Enable(TTY_Enable), .halt(halt), .SelectorCodes(SelectorCodes), .S_FC(FC_Selector), .pop(Pop),
    .push(Push), .load(Load), .store(Store), .Main_In(ReadInstruction), .Main_Out(Main),
    .kbd_Enable(kbd_Enable));
  or or_9 (ChipSelect, CS4, CS3, CS2, CS1, CS0);

  assign RESET = START;

  // Other names for the same wires on the sheet: Chip_Select = ChipSelect; clk = Clock; ReadIns = ReadInstruction;
  //   Selector_Codes[17:0] = SelectorCodes

  // Notes on the sheet:
  //   Input_Output_Region
  //   Instruction-Lines
endmodule
